// Logisim project 2019_dg_p1.circ as structural Verilog: 1 circuit, main circuit main
module main (
);

  wire A_out, B_out, C_out, nand_1_out, not_1_out, xor_1_out;

  Button A (.out(A_out));
  Button B (.out(B_out));
  Button C (.out(C_out));
  not not_1 (not_1_out, A_out);
  xor xor_1 (xor_1_out, not_1_out, B_out);
  nand nand_1 (nand_1_out, xor_1_out, C_out);
  LED S (.in(nand_1_out));
endmodule
